// Logisim project DFF.circ as structural Verilog: 1 circuit, main circuit main
module main (
);

  wire and_1_out, and_2_out, clock_1_out, D, E, not_1_out, nQ, Q;

  Clock clock_1 (.out(clock_1_out));
  and and_1 (and_1_out, clock_1_out, not_1_out, E);
  not not_1 (not_1_out, D);
  and and_2 (and_2_out, E, D, clock_1_out);
  nor nor_1 (Q, and_1_out, nQ);
  nor nor_2 (nQ, Q, and_2_out);
endmodule
