// Logisim project FIB COUNTER (HEX DISPLAY AND BCD ON 3x 7 SEG.circ as structural Verilog: 4 circuits, main circuit main
module main (
  input  MANUAL_RESET,
  input  PAUSE
);

  wire and_1_out, clock_1_out, Count_Enable, or_2_out, PAUSE_t, RESET;
  wire [7:0] adder_1_out, CURRENT_q, multiplexer_1_out, multiplexer_2_out, multiplexer_3_out, PREVIOUS_q,
       RESET_REGISTER__PERMANENTLY_ZERO_q;
  wire [7:7] not_2_out;

  Clock clock_1 (.out(clock_1_out));
  not not_1 (PAUSE_t, PAUSE);
  not not_2 (not_2_out[7], Count_Enable);
  Multiplexer #(.width(8)) multiplexer_1 (
    .in0({{7{not_2_out[7]}}, Count_Enable}), .in1(adder_1_out), .out(multiplexer_1_out), .sel(or_2_out));  // open: en
  Multiplexer #(.width(8)) multiplexer_2 (
    .in0(multiplexer_1_out), .in1(RESET_REGISTER__PERMANENTLY_ZERO_q), .out(multiplexer_2_out), .sel(RESET));  // open: en
  Register CURRENT (.D(multiplexer_2_out), .en(PAUSE_t), .Q(CURRENT_q), .clk(clock_1_out));  // open: clr
  Hex_Digit_Display hex_digit_display_1 (.value(CURRENT_q[3:0]));  // open: dp
  Hex_Digit_Display hex_digit_display_2 (.value(CURRENT_q[7:4]));  // open: dp
  Register RESET_REGISTER__PERMANENTLY_ZERO (
    .D(RESET_REGISTER__PERMANENTLY_ZERO_q), .Q(RESET_REGISTER__PERMANENTLY_ZERO_q), .clk(clock_1_out));  // open: en, clr
  Multiplexer #(.width(8)) multiplexer_3 (
    .in0(CURRENT_q), .in1(RESET_REGISTER__PERMANENTLY_ZERO_q), .out(multiplexer_3_out), .sel(RESET));  // open: en
  Register PREVIOUS (.D(multiplexer_3_out), .en(PAUSE_t), .Q(PREVIOUS_q), .clk(clock_1_out));  // open: clr
  Adder adder_1 (.a(CURRENT_q), .b(PREVIOUS_q), .out(adder_1_out));  // open: cin, cout
  and and_1 (and_1_out, CURRENT_q[0], CURRENT_q[3], CURRENT_q[5], CURRENT_q[6], CURRENT_q[7]);
  or or_1 (RESET, MANUAL_RESET, and_1_out);
  or or_2 (or_2_out, PREVIOUS_q[0], PREVIOUS_q[1], PREVIOUS_q[2], PREVIOUS_q[3], PREVIOUS_q[4], PREVIOUS_q[5], PREVIOUS_q[6], PREVIOUS_q[7]);
  not not_3 (Count_Enable, or_2_out);
endmodule

module BCD (
  input  [11:0] in_1,
  input  MANUAL_RESET,
  input  PAUSE
);

  wire A1, A2, A3, A4, A5, A6, A7, B1, B2, B3, B4, B5, B6, B7, C1, C2, C3, C4, C5, C6, C7, clock_1_out,
       comparator_1_eq, not_1_out, or_1_out, RESET;
  wire [3:0] LSBs, MIDDLE, MSBs;
  wire [11:0] multiplexer_1_out, PREV_q, SUM;

  Clock clock_1 (.out(clock_1_out));
  Comparator #(.width(12), .mode("unsigned")) comparator_1 (
    .a({MSBs, MIDDLE, LSBs}), .b(in_1), .eq(comparator_1_eq));  // open: gt, lt
  or or_1 (or_1_out, RESET, MANUAL_RESET);
  not not_1 (not_1_out, PAUSE);
  Multiplexer #(.width(12)) multiplexer_1 (
    .in0(SUM), .in1(12'h1), .out(multiplexer_1_out), .sel(comparator_1_eq));  // open: en
  Register #(.width(12)) PREV (.D({MSBs, MIDDLE, LSBs}), .en(not_1_out), .Q(PREV_q), .clk(clock_1_out), .clr(or_1_out));
  Register #(.width(12)) NEXT (
    .D(multiplexer_1_out), .en(not_1_out), .Q({MSBs, MIDDLE, LSBs}), .clk(clock_1_out), .clr(or_1_out));
  _7_Segment_Display u_7_segment_display_1 (.g(A1), .f(A2), .a(A3), .b(A4), .e(A7), .d(A6), .c(A5));  // open: dp
  _7_Segment_Display u_7_segment_display_2 (.g(C1), .f(C2), .a(C3), .b(C4), .e(C7), .d(C6), .c(C5));  // open: dp
  _7_Segment_Display u_7_segment_display_3 (.g(B1), .f(B2), .a(B3), .b(B4), .e(B7), .d(B6), .c(B5));  // open: dp
  BCD_ADDITION bcd_addition_1 (
    .in_1(LSBs[0]), .in_2(LSBs[1]), .in_3(LSBs[2]), .in_4(LSBs[3]), .in_5(PREV_q[0]), .in_6(PREV_q[1]),
    .in_7(PREV_q[2]), .in_8(PREV_q[3]), .in_9(MIDDLE[0]), .in_10(MIDDLE[1]), .in_11(MIDDLE[2]),
    .in_12(MIDDLE[3]), .in_13(PREV_q[4]), .in_14(PREV_q[5]), .in_15(PREV_q[6]), .in_16(PREV_q[7]),
    .in_17(MSBs[0]), .in_18(MSBs[1]), .in_19(MSBs[2]), .in_20(MSBs[3]), .in_21(PREV_q[8]), .in_22(PREV_q[9]),
    .in_23(PREV_q[10]), .in_24(PREV_q[11]), .A1(SUM[0]), .A2(SUM[1]), .A3(SUM[2]), .A4(SUM[3]), .B1(SUM[4]),
    .B2(SUM[5]), .B3(SUM[6]), .B4(SUM[7]), .C1(SUM[8]), .C2(SUM[9]), .C3(SUM[10]), .C4(SUM[11]));
  and and_1 (RESET, SUM[4], SUM[9], SUM[10]);
  _7_SEG u_7_seg_1 (
    .W(MSBs[3]), .X(MSBs[2]), .Y(MSBs[1]), .Z(MSBs[0]), ._7(A7), ._6(A6), ._5(A5), ._1(A1), ._2(A2), ._3(A3),
    ._4(A4));
  _7_SEG u_7_seg_2 (
    .W(MIDDLE[3]), .X(MIDDLE[2]), .Y(MIDDLE[1]), .Z(MIDDLE[0]), ._7(B7), ._6(B6), ._5(B5), ._1(B1), ._2(B2),
    ._3(B3), ._4(B4));
  _7_SEG u_7_seg_3 (
    .W(LSBs[3]), .X(LSBs[2]), .Y(LSBs[1]), .Z(LSBs[0]), ._7(C7), ._6(C6), ._5(C5), ._1(C1), ._2(C2), ._3(C3),
    ._4(C4));
endmodule

module BCD_ADDITION (
  input  in_1,
  input  in_2,
  input  in_3,
  input  in_4,
  input  in_5,
  input  in_6,
  input  in_7,
  input  in_8,
  input  in_9,
  input  in_10,
  input  in_11,
  input  in_12,
  input  in_13,
  input  in_14,
  input  in_15,
  input  in_16,
  input  in_17,
  input  in_18,
  input  in_19,
  input  in_20,
  input  in_21,
  input  in_22,
  input  in_23,
  input  in_24,
  output A1,
  output A2,
  output A3,
  output A4,
  output B1,
  output B2,
  output B3,
  output B4,
  output C1,
  output C2,
  output C3,
  output C4
);

  wire comparator_1_eq, comparator_1_gt, comparator_1_lt, comparator_2_eq, comparator_2_gt, comparator_2_lt,
       or_1_out, or_2_out;
  wire [3:0] adder_1_out, adder_2_out, subtractor_1_out, subtractor_2_out;

  Adder #(.width(4)) adder_1 (
    .a({in_4, in_3, in_2, in_1}), .b({in_8, in_7, in_6, in_5}), .out(adder_1_out));  // open: cin, cout
  Adder #(.width(4)) adder_2 (
    .a({in_12, in_11, in_10, in_9}), .b({in_16, in_15, in_14, in_13}), .out(adder_2_out), .cin(or_1_out));  // open: cout
  Adder #(.width(4)) adder_3 (
    .a({in_20, in_19, in_18, in_17}), .b({in_24, in_23, in_22, in_21}), .out({C4, C3, C2, C1}), .cin(or_2_out));  // open: cout
  Subtractor #(.width(4)) subtractor_1 (.a(adder_1_out), .b(4'b1010), .out(subtractor_1_out));  // open: bin, bout
  Comparator #(.width(4), .mode("unsigned")) comparator_1 (
    .a(adder_1_out), .b(4'b1010), .gt(comparator_1_gt), .eq(comparator_1_eq), .lt(comparator_1_lt));
  Comparator #(.width(4), .mode("unsigned")) comparator_2 (
    .a(adder_2_out), .b(4'b1010), .gt(comparator_2_gt), .eq(comparator_2_eq), .lt(comparator_2_lt));
  or or_1 (or_1_out, comparator_1_gt, comparator_1_eq);
  or or_2 (or_2_out, comparator_2_gt, comparator_2_eq);
  Subtractor #(.width(4)) subtractor_2 (.a(adder_2_out), .b(4'b1010), .out(subtractor_2_out));  // open: bin, bout
  Multiplexer #(.width(4)) multiplexer_1 (
    .in0(subtractor_1_out), .in1(adder_1_out), .out({A4, A3, A2, A1}), .sel(comparator_1_lt));  // open: en
  Multiplexer #(.width(4)) multiplexer_2 (
    .in0(subtractor_2_out), .in1(adder_2_out), .out({B4, B3, B2, B1}), .sel(comparator_2_lt));  // open: en
endmodule

module _7_SEG (
  input  W,
  input  X,
  input  Y,
  input  Z,
  output _1,
  output _2,
  output _3,
  output _4,
  output _7,
  output _6,
  output _5
);

  wire _8, and_1_out, and_2_out, and_3_out, and_4_out, and_5_out, and_6_out, and_7_out, and_8_out, and_9_out,
       and_10_out, and_11_out, and_12_out, and_13_out, and_14_out, and_15_out, and_16_out, and_17_out,
       and_18_out, and_19_out, and_20_out, and_21_out, and_22_out, and_23_out, or_1_out, or_4_out, or_8_out,
       or_10_out, or_12_out, or_13_out, W_prime, X_prime, xor_1_out, xor_2_out, xor_3_out, Y_prime, Z_prime;

  and and_1 (and_1_out, Y, or_1_out);
  or or_1 (or_1_out, and_2_out, and_3_out, W);
  and and_2 (and_2_out, W_prime, X_prime);
  and and_3 (and_3_out, W_prime, Z_prime);
  or or_2 (_1, and_1_out, and_5_out, and_4_out);
  and and_4 (and_4_out, W_prime, X, Y_prime);
  and and_5 (and_5_out, W, X_prime);
  and and_6 (and_6_out, Z_prime, X, Y);
  or or_3 (_2, and_6_out, W, and_7_out);
  and and_7 (and_7_out, or_4_out, Y_prime);
  or or_4 (or_4_out, X, Z_prime);
  or or_5 (_3, W, Y, and_9_out, and_8_out);
  and and_8 (and_8_out, X_prime, Y_prime, Z_prime);
  and and_9 (and_9_out, X, Z);
  and and_10 (and_10_out, W_prime, Y_prime, Z_prime);
  or or_6 (_4, and_10_out, X_prime, and_11_out);
  and and_11 (and_11_out, xor_1_out, Z);
  xor xor_1 (xor_1_out, W, Y);
  not not_1 (W_prime, W);
  xor xor_2 (xor_2_out, W, X);
  not not_2 (X_prime, X);
  or or_7 (_5, xor_2_out, and_13_out, and_12_out);
  and and_12 (and_12_out, W_prime, Y, Z);
  and and_13 (and_13_out, Y_prime, or_8_out);
  or or_8 (or_8_out, W_prime, Z);
  not not_3 (Y_prime, Y);
  and and_14 (and_14_out, X, xor_3_out);
  xor xor_3 (xor_3_out, Y, Z);
  not not_4 (Z_prime, Z);
  or or_9 (_6, and_14_out, and_15_out, and_16_out);
  and and_15 (and_15_out, X_prime, or_10_out);
  and and_16 (and_16_out, W, Y_prime);
  or or_10 (or_10_out, and_17_out, and_19_out, and_18_out);
  and and_17 (and_17_out, W, Z);
  and and_18 (and_18_out, Y_prime, Z_prime);
  and and_19 (and_19_out, W_prime, Y);
  or or_11 (_7, and_20_out, and_21_out);
  and and_20 (and_20_out, Z_prime, or_12_out);
  or or_12 (or_12_out, Y, X_prime);
  and and_21 (and_21_out, W, or_13_out);
  or or_13 (or_13_out, X, Y);
  and and_22 (and_22_out, W, X_prime, Y, Z);
  or or_14 (_8, and_22_out, and_23_out);
  and and_23 (and_23_out, W, X, Y_prime, Z);
endmodule
