// Logisim project GRAY COUNTER.circ as structural Verilog: 1 circuit, main circuit main
module main (
  output out_1,
  output out_2,
  output out_3
);

  wire A_prime, and_1_out, and_2_out, and_3_out, and_4_out, and_5_out, and_6_out, B_prime, C_prime,
       clock_1_out, or_1_out, xor_1_out;

  and and_1 (and_1_out, out_2, C_prime);
  and and_2 (and_2_out, B_prime, C_prime);
  Clock clock_1 (.out(clock_1_out));
  J_K_Flip_Flop _0 (.J(and_1_out), .clk(clock_1_out), .K(and_2_out), .Q(out_1));  // open: Qn, preset, en, reset
  and and_3 (and_3_out, A_prime, out_3);
  J_K_Flip_Flop _1 (.J(and_3_out), .clk(clock_1_out), .K(and_4_out), .Q(out_2));  // open: Qn, preset, en, reset
  and and_4 (and_4_out, out_1, out_3);
  xor xor_1 (xor_1_out, out_1, out_2);
  not not_1 (A_prime, out_1);
  not not_2 (B_prime, out_2);
  not not_3 (C_prime, out_3);
  J_K_Flip_Flop _2 (.J(or_1_out), .clk(clock_1_out), .K(xor_1_out), .Q(out_3));  // open: Qn, preset, en, reset
  or or_1 (or_1_out, and_5_out, and_6_out);
  and and_5 (and_5_out, A_prime, B_prime);
  and and_6 (and_6_out, out_1, out_2);

  // Other names for the same wires on the sheet: A = out_1; B = out_2; C = out_3
endmodule
