// Logisim project PROC.circ as structural Verilog: 4 circuits, main circuit main
module main (
  input  in_1,
  input  in_2,
  input  in_3,
  input  in_4,
  input  in_5,
  input  [31:0] in_6,
  output [31:0] out_7
);

  D_FF d_ff_1 ();  // open: D, E, Q, nQ
  Clock clock_1 ();  // open: out
  REG_FILE reg_file_1 (
    .D_IN(in_6), .IN4(in_1), .IN3(in_2), .IN2(in_3), .IN1(in_4), .IN0(in_5), .R19(out_7));  // open: R0, R1, R2, R3, R4, R5, R6, R7, R8, R9, R10, R11, R12, R13, R14, R15, R16, R17, R18, R20, R21, R22, R23, R24, R25, R26, R27, R28, R29, R30, TEMPR
endmodule

module D_FF (
  input  D,
  input  E,
  output Q,
  output nQ
);

  wire and_1_out, and_2_out, CLK, not_1_out;

  and and_1 (and_1_out, CLK, not_1_out, E);
  not not_1 (not_1_out, D);
  and and_2 (and_2_out, E, D, CLK);
  Clock clock_1 (.out(CLK));
  nor nor_1 (Q, and_1_out, nQ);
  nor nor_2 (nQ, Q, and_2_out);
endmodule

module REG (
  input  LOAD,
  input  [31:0] D,
  output [31:0] Q
);

  D_FF d_ff_1 (.D(D[0]), .E(LOAD), .Q(Q[0]));  // open: nQ
  D_FF d_ff_2 (.D(D[1]), .E(LOAD), .Q(Q[1]));  // open: nQ
  D_FF d_ff_3 (.D(D[2]), .E(LOAD), .Q(Q[2]));  // open: nQ
  D_FF d_ff_4 (.D(D[3]), .E(LOAD), .Q(Q[3]));  // open: nQ
  D_FF d_ff_5 (.D(D[4]), .E(LOAD), .Q(Q[4]));  // open: nQ
  D_FF d_ff_6 (.D(D[5]), .E(LOAD), .Q(Q[5]));  // open: nQ
  D_FF d_ff_7 (.D(D[6]), .E(LOAD), .Q(Q[6]));  // open: nQ
  D_FF d_ff_8 (.D(D[7]), .E(LOAD), .Q(Q[7]));  // open: nQ
  D_FF d_ff_9 (.D(D[8]), .E(LOAD), .Q(Q[8]));  // open: nQ
  D_FF d_ff_10 (.D(D[9]), .E(LOAD), .Q(Q[9]));  // open: nQ
  D_FF d_ff_11 (.D(D[10]), .E(LOAD), .Q(Q[10]));  // open: nQ
  D_FF d_ff_12 (.D(D[11]), .E(LOAD), .Q(Q[11]));  // open: nQ
  D_FF d_ff_13 (.D(D[12]), .E(LOAD), .Q(Q[12]));  // open: nQ
  D_FF d_ff_14 (.D(D[13]), .E(LOAD), .Q(Q[13]));  // open: nQ
  D_FF d_ff_15 (.D(D[14]), .E(LOAD), .Q(Q[14]));  // open: nQ
  D_FF d_ff_16 (.D(D[15]), .E(LOAD), .Q(Q[15]));  // open: nQ
  D_FF d_ff_17 (.D(D[16]), .E(LOAD), .Q(Q[16]));  // open: nQ
  D_FF d_ff_18 (.D(D[17]), .E(LOAD), .Q(Q[17]));  // open: nQ
  D_FF d_ff_19 (.D(D[18]), .E(LOAD), .Q(Q[18]));  // open: nQ
  D_FF d_ff_20 (.D(D[19]), .E(LOAD), .Q(Q[19]));  // open: nQ
  D_FF d_ff_21 (.D(D[20]), .E(LOAD), .Q(Q[20]));  // open: nQ
  D_FF d_ff_22 (.D(D[21]), .E(LOAD), .Q(Q[21]));  // open: nQ
  D_FF d_ff_23 (.D(D[22]), .E(LOAD), .Q(Q[22]));  // open: nQ
  D_FF d_ff_24 (.D(D[23]), .E(LOAD), .Q(Q[23]));  // open: nQ
  Clock CLOCK ();  // open: out
  D_FF d_ff_25 (.D(D[24]), .E(LOAD), .Q(Q[24]));  // open: nQ
  D_FF d_ff_26 (.D(D[25]), .E(LOAD), .Q(Q[25]));  // open: nQ
  D_FF d_ff_27 (.D(D[26]), .E(LOAD), .Q(Q[26]));  // open: nQ
  D_FF d_ff_28 (.D(D[27]), .E(LOAD), .Q(Q[27]));  // open: nQ
  D_FF d_ff_29 (.D(D[28]), .E(LOAD), .Q(Q[28]));  // open: nQ
  D_FF d_ff_30 (.D(D[29]), .E(LOAD), .Q(Q[29]));  // open: nQ
  D_FF d_ff_31 (.D(D[30]), .E(LOAD), .Q(Q[30]));  // open: nQ
  D_FF d_ff_32 (.D(D[31]), .E(LOAD), .Q(Q[31]));  // open: nQ

  // Other names for the same wires on the sheet: D0_3[3:0] = D[3:0]; D4_7[3:0] = D[7:4]; D8_B[3:0] = D[11:8];
  //   DA = D[10]; DB = D[11]; DC = D[12]; DC_F[3:0] = D[15:12]; DD = D[13]; DE = D[14]; DF = D[15]; D10 = D[16];
  //   D10_13[3:0] = D[19:16]; D11 = D[17]; D12 = D[18]; D13 = D[19]; D14 = D[20]; D14_17[3:0] = D[23:20]; D15 = D[21];
  //   D16 = D[22]; D17 = D[23]; D18 = D[24]; D18_1B[3:0] = D[27:24]; D19 = D[25]; D1A = D[26]; D1B = D[27];
  //   D1C = D[28]; D1C_1F[3:0] = D[31:28]; D1D = D[29]; D1E = D[30]; D1F = D[31]; Q0_3[3:0] = Q[3:0];
  //   Q4_7[3:0] = Q[7:4]; Q8_B[3:0] = Q[11:8]; QC_F[3:0] = Q[15:12]; Q10_13[3:0] = Q[19:16]; Q14_17[3:0] = Q[23:20];
  //   Q18_1B[3:0] = Q[27:24]; Q1C_1F[3:0] = Q[31:28]
endmodule

module REG_FILE (
  input  IN4,
  input  IN3,
  input  IN2,
  input  IN1,
  input  IN0,
  input  [31:0] D_IN,
  output [31:0] R0,
  output [31:0] R1,
  output [31:0] R2,
  output [31:0] R3,
  output [31:0] R4,
  output [31:0] R5,
  output [31:0] R6,
  output [31:0] R7,
  output [31:0] R8,
  output [31:0] R9,
  output [31:0] R10,
  output [31:0] R11,
  output [31:0] R12,
  output [31:0] R13,
  output [31:0] R14,
  output [31:0] R15,
  output [31:0] R16,
  output [31:0] R17,
  output [31:0] R18,
  output [31:0] R19,
  output [31:0] R20,
  output [31:0] R21,
  output [31:0] R22,
  output [31:0] R23,
  output [31:0] R24,
  output [31:0] R25,
  output [31:0] R26,
  output [31:0] R27,
  output [31:0] R28,
  output [31:0] R29,
  output [31:0] R30,
  output [31:0] TEMPR
);

  wire L0, L1, L2, L3, L4, L5, L6, L7, L8, L9, L10, L11, L12, L13, L14, L15, L16, L17, L18, L19, L20, L21,
       L22, L23, L24, L25, L26, L27, L28, L29, L30, LTMP, nIN0, nIN1, nIN2, nIN3, nIN4;

  REG u_R8 (.D(D_IN), .LOAD(L8), .Q(R8));
  REG u_R12 (.D(D_IN), .LOAD(L12), .Q(R12));
  REG u_R16 (.D(D_IN), .LOAD(L16), .Q(R16));
  REG u_R20 (.D(D_IN), .LOAD(L20), .Q(R20));
  REG u_R24 (.D(D_IN), .LOAD(L24), .Q(R24));
  REG u_R28 (.D(D_IN), .LOAD(L28), .Q(R28));
  REG u_R0 (.D(D_IN), .LOAD(L0), .Q(R0));
  REG u_R4 (.D(D_IN), .LOAD(L4), .Q(R4));
  REG u_R9 (.D(D_IN), .LOAD(L9), .Q(R9));
  REG u_R13 (.D(D_IN), .LOAD(L13), .Q(R13));
  REG u_R17 (.D(D_IN), .LOAD(L17), .Q(R17));
  REG u_R21 (.D(D_IN), .LOAD(L21), .Q(R21));
  REG u_R25 (.D(D_IN), .LOAD(L25), .Q(R25));
  REG u_R29 (.D(D_IN), .LOAD(L29), .Q(R29));
  REG u_R1 (.D(D_IN), .LOAD(L1), .Q(R1));
  REG u_R5 (.D(D_IN), .LOAD(L5), .Q(R5));
  REG u_R10 (.D(D_IN), .LOAD(L10), .Q(R10));
  REG u_R14 (.D(D_IN), .LOAD(L14), .Q(R14));
  REG u_R18 (.D(D_IN), .LOAD(L18), .Q(R18));
  REG u_R22 (.D(D_IN), .LOAD(L22), .Q(R22));
  REG u_R26 (.D(D_IN), .LOAD(L26), .Q(R26));
  REG u_R30 (.D(D_IN), .LOAD(L30), .Q(R30));
  REG u_R2 (.D(D_IN), .LOAD(L2), .Q(R2));
  REG u_R6 (.D(D_IN), .LOAD(L6), .Q(R6));
  REG u_R11 (.D(D_IN), .LOAD(L11), .Q(R11));
  REG u_R15 (.D(D_IN), .LOAD(L15), .Q(R15));
  REG u_R19 (.D(D_IN), .LOAD(L19), .Q(R19));
  REG u_R23 (.D(D_IN), .LOAD(L23), .Q(R23));
  REG u_R27 (.D(D_IN), .LOAD(L27), .Q(R27));
  REG u_TEMPR (.D(D_IN), .LOAD(LTMP), .Q(TEMPR));
  REG u_R3 (.D(D_IN), .LOAD(L3), .Q(R3));
  REG u_R7 (.D(D_IN), .LOAD(L7), .Q(R7));
  not not_1 (nIN4, IN4);
  not not_2 (nIN3, IN3);
  Clock clock_1 ();  // open: out
  not not_3 (nIN2, IN2);
  not not_4 (nIN1, IN1);
  not not_5 (nIN0, IN0);
  and and_1 (L0, nIN4, nIN3, nIN2, nIN1, nIN0);
  and and_2 (L4, nIN4, nIN3, IN2, nIN1, nIN0);
  and and_3 (L8, nIN4, IN3, nIN2, nIN1, nIN0);
  and and_4 (L12, nIN4, IN3, IN2, nIN1, nIN0);
  and and_5 (L16, IN4, nIN3, nIN2, nIN1, nIN0);
  and and_6 (L20, IN4, nIN3, IN2, nIN1, nIN0);
  and and_7 (L24, IN4, IN3, nIN2, nIN1, nIN0);
  and and_8 (L28, IN4, IN3, IN2, nIN1, nIN0);
  and and_9 (L1, nIN4, nIN3, nIN2, nIN1, IN0);
  and and_10 (L5, nIN4, nIN3, IN2, nIN1, IN0);
  and and_11 (L9, nIN4, IN3, nIN2, nIN1, IN0);
  and and_12 (L13, nIN4, IN3, IN2, nIN1, IN0);
  and and_13 (L17, IN4, nIN3, nIN2, nIN1, IN0);
  and and_14 (L21, IN4, nIN3, IN2, nIN1, IN0);
  and and_15 (L25, IN4, IN3, nIN2, nIN1, IN0);
  and and_16 (L29, IN4, IN3, IN2, nIN1, IN0);
  and and_17 (L2, nIN4, nIN3, nIN2, IN1, nIN0);
  and and_18 (L6, nIN4, nIN3, IN2, IN1, nIN0);
  and and_19 (L10, nIN4, IN3, nIN2, IN1, nIN0);
  and and_20 (L14, nIN4, IN3, IN2, IN1, nIN0);
  and and_21 (L18, IN4, nIN3, nIN2, IN1, nIN0);
  and and_22 (L22, IN4, nIN3, IN2, IN1, nIN0);
  and and_23 (L26, IN4, IN3, nIN2, IN1, nIN0);
  and and_24 (L30, IN4, IN3, IN2, IN1, nIN0);
  and and_25 (L3, nIN4, nIN3, nIN2, IN1, IN0);
  and and_26 (L7, nIN4, nIN3, IN2, IN1, IN0);
  and and_27 (L11, nIN4, IN3, nIN2, IN1, IN0);
  and and_28 (L15, nIN4, IN3, IN2, IN1, IN0);
  and and_29 (L19, IN4, nIN3, nIN2, IN1, IN0);
  and and_30 (L23, IN4, nIN3, IN2, IN1, IN0);
  and and_31 (L27, IN4, IN3, nIN2, IN1, IN0);
  and and_32 (LTMP, IN4, IN3, IN2, IN1, IN0);

  // Other names for the same wires on the sheet: D[31:0] = D_IN; R0Q[31:0] = R0; R1Q[31:0] = R1; R2Q[31:0] = R2;
  //   R3Q[31:0] = R3; R4Q[31:0] = R4; R5Q[31:0] = R5; R6Q[31:0] = R6; R7Q[31:0] = R7; R8Q[31:0] = R8; R9Q[31:0] = R9;
  //   R10Q[31:0] = R10; R11Q[31:0] = R11; R12Q[31:0] = R12; R13Q[31:0] = R13; R14Q[31:0] = R14; R15Q[31:0] = R15;
  //   R16Q[31:0] = R16; R17Q[31:0] = R17; R18Q[31:0] = R18; R19Q[31:0] = R19; R20Q[31:0] = R20; R21Q[31:0] = R21;
  //   R22Q[31:0] = R22; R23Q[31:0] = R23; R24Q[31:0] = R24; R25Q[31:0] = R25; R26Q[31:0] = R26; R27Q[31:0] = R27;
  //   R28Q[31:0] = R28; R29Q[31:0] = R29; R30Q[31:0] = R30; TEMPRQ[31:0] = TEMPR
endmodule
